# Fritzing sketch ESP_white_LED (saved by Fritzing 0.8.7b)
circuit board: 8.46667cm x 5.64444cm
breadboards: 1

parts:
  ESP = ESP8266 WiFi Module [part_number=ESP8266]
  12v_In = Power Jack [package=power_jack_pth]
  U1 = Voltage Regulator -- 3.3 V -- LM1117
  irlz34n = Basic FET N-Channel [package="DPak [SMD]"]
  LED_Out = female pin header, 4 pins [form="♀ (female)"]
  Led_Strip = female pin header, 4 pins [form="♀ (female)"]
  R1 = Resistor [tolerance=±5% resistance=220 package=THT]

nets:
  N1: ESP.RXD, irlz34n.Gate, R1.Pin_0
  N2: ESP.VCC, ESP.RST, ESP.CH_PD, U1.OUT
  GND: ESP.GND, 12v_In.GND, 12v_In.GNDBREAK, U1.GND, irlz34n.source, R1.Pin_1
  N3: 12v_In.PWR, U1.IN, LED_Out.pin1, Led_Strip.pin1
  N4: irlz34n.drain, LED_Out.pin4, Led_Strip.pin4
  N5: LED_Out.pin2, Led_Strip.pin2
  N6: LED_Out.pin3, Led_Strip.pin3

notes:
  12v Rail
  3.3v Rail

custom parts:
  ESP8266 WiFi Module: Generic WiFi Module based on the ESP8266 with onboard PCB antenna and UART communications
  Voltage Regulator -- 3.3 V -- LM1117: LM1117-3.3 Voltage regulator, 3.3 V output. Note that the pinout order is not the same as LM7805 or LM7833.
